# Fritzing sketch board-v1 (saved by Fritzing 1.0.7)
circuit board: 5.63909cm x 4.41668cm
stripboards: 1

parts:
  L_sens_SL_N = Camdenboss CTB0158-3 [part_number=CTB0158-3 package=THT]
  L_in_N = Camdenboss CTB0158-2 [part_number=CTB0158-2 package=THT]
  L_out_N = Camdenboss CTB0158-2 [part_number=CTB0158-2 package=THT]
  U1 = 888H-1CC-F-C E [part_number="888H-1CC-F-C E"]
  J1_(Sonoff) = Camdenboss CTB0158-6 [part_number=CTB0158-6 package=THT]
  F1_(0_2A) = FUSE [package=fuse_5mm]

nets:
  N1: L_sens_SL_N.pin1, U1.14_COM, J1_(Sonoff).pin4, J1_(Sonoff).pin5, F1_(0_2A).2
  N2: L_sens_SL_N.pin2, U1.22_-
  N3: L_sens_SL_N.pin3, L_in_N.pin2, L_out_N.pin2, U1.1_+, J1_(Sonoff).pin1, J1_(Sonoff).pin2
  N4: L_in_N.pin1, F1_(0_2A).1
  N5: L_out_N.pin1, J1_(Sonoff).pin3
  N6: U1.12_N.O., J1_(Sonoff).pin6
