# Fritzing sketch board-v2 (saved by Fritzing 1.0.7)
circuit board: 6.74162cm x 4.44841cm
stripboards: 1

parts:
  L_sens_SL_N = Camdenboss CTB0158-3 [part_number=CTB0158-3 package=THT]
  L_in_N = Camdenboss CTB0158-2 [part_number=CTB0158-2 package=THT]
  J1_(Sonoff) = Camdenboss CTB0158-6 [part_number=CTB0158-6 package=THT]
  F1_(0_2A) = FUSE [package=fuse_5mm]
  U1 = 888H-1CC-F-C E [part_number="888H-1CC-F-C E"]
  L_out_N = Camdenboss CTB0158-2 [part_number=CTB0158-2 package=THT]
  C1 = Film/Foil Capacitor [capacitance=100nF voltage=35V package="15mm [THT, pp]"]
  D1 = LED - 5mm [color="Red (633nm)" current=0.030A package="5 mm [THT]"]

nets:
  N1: L_sens_SL_N.pin1, J1_(Sonoff).pin4, J1_(Sonoff).pin5, F1_(0_2A).2, U1.14_COM, C1.+
  N2: L_sens_SL_N.pin2, U1.22_-
  N3: L_sens_SL_N.pin3, L_in_N.pin2, J1_(Sonoff).pin1, J1_(Sonoff).pin2, U1.1_+, L_out_N.pin2, D1.cathode
  N4: L_in_N.pin1, F1_(0_2A).1
  N5: J1_(Sonoff).pin3, L_out_N.pin1
  N6: J1_(Sonoff).pin6, U1.12_N.O.
  N7: C1.-, D1.anode

notes:
  SLIP 2.0
